# Fritzing sketch Robot_Mower (saved by Fritzing 0.9.3b)
breadboards: 1

parts:
  Raspberry_Pi_1 = Raspberry Pi 3 [part_number=RPI-3-V1.2]
  MPU9250_MPU-1 = SparkFun IMU Breakout - MPU-9250 [part_number=" SEN-13762"]
  Part1 = INA219 High Side DC Current Sensor Breakout [part_number=904]
  LED1 = RGB LED (com. cathode, rbg) [package="5 mm [THT]"]  # not connected
  LED2 = RGB LED (com. cathode, rbg) [package="5 mm [THT]"]  # not connected
  Part2 = IBT_2  # not connected

nets:
  3V3: Raspberry_Pi_1.3v3, MPU9250_MPU-1.VDD, Part1.VCC
  N1: Raspberry_Pi_1.GPIO2, MPU9250_MPU-1.SDA/SDI, Part1.SDA, Part1.VIN-
  N2: Raspberry_Pi_1.GPIO3, MPU9250_MPU-1.SCL/SCLK, Part1.SCL
  GND: Raspberry_Pi_1.GND, MPU9250_MPU-1.GND, Part1.GND

custom parts:
  INA219 High Side DC Current Sensor Breakout: This breakout board will solve all your power-monitoring problems. Instead of struggling with two multimeters, you can just use the handy INA219B chip on this breakout to both measure both the high side voltage and DC current draw over I2C with 1% precision. Most current-measuring devices such as our current panel meter are only good for low side measuring. That means that unless you want to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
